# Fritzing sketch breadboard_diagram (saved by Fritzing 1.0.3b)

parts:
  L298N1 = L298N DC motor driver
  Part1 = STM32F407G-DISC1
  M1 = DC Motor [voltage_(max)=6V voltage_(min)=3V]  # not connected
  Part2 = InvenSense MPU6050

nets:
  N1: L298N1.5V, Part1.pin82
  N2: L298N1.IN1, Part1.pin4
  N3: L298N1.IN2, Part1.pin30
  N4: Part1.pin1, Part1.pin3, Part2.GND
  N5: Part1.pin2, Part2.VCC
  N6: Part1.pin72, Part2.SCL
  N7: Part1.pin98, Part2.SDA

custom parts:
  L298N DC motor driver: 2x DC motor driver with 78M05 positive voltage regulator (7..35 V) L298N: max 46 V, 2 A Set 5 V Enable jumper to enable 5 V regultor (needed for the L298N) and +5 V output at screw terminal or supply external +5 V at screw terminal Set ENA and/or ENB to +5 V to enable motor permanently or supply ENA and/or ENB with PWM signal IN1 and IN2 set rotation directory for motor A (OUT1/OUT2) IN2 and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
  STM32F407G-DISC1: The STM32F4DISCOVERY Discovery kit allows users to easily develop applications with the STM32F407VG high-performance microcontroller with the Arm® Cortex®-M4 32-bit core. It includes everything required either for beginners or experienced users to get started quickly. Based on STM32F407VG, it includes an ST-LINK/V2-A embedded debug tool, one STMEMS digital accelerometer, one digital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
